# Fritzing sketch GearDCwPotBC547 (saved by Fritzing 0.9.3b)
breadboards: 1

parts:
  T3_Vakfı1 = Generic shrouded header - 32 pins [package=THT]
  M1 = Getriebemotor
  Q1 = NPN-Transistor [part_number=BC547 package="SOT-23 [SMD]"]
  D1 = Rectifier Diode [part_number=1N4001 package="300 mil [THT]"]
  R1 = Resistor [tolerance=±5% resistance=10k package=THT]
  U1 = POT [package=alps_pot]  # not connected

nets:
  N1: T3_Vakfı1.pin13, R1.Pin_0
  N2: T3_Vakfı1.pin15, M1.pin_2, D1.cathode
  N3: T3_Vakfı1.pin16, Q1.1
  N4: M1.pin_1, Q1.2, D1.anode
  N5: Q1.0, R1.Pin_1

custom parts:
  Generic shrouded header - 32 pins: Ülkemizin mühendislik kaynakları kullanılarak geliştirilen Deneyap Kart; güçlü işlemcisi, dayanıklı tasarımı ve çok yönlü giriş/çıkış pinleri ile kullanıcılara Elektronik Programlama, Nesnelerin İnterneti (IoT) ve Yapay Zeka alanlarında başlangıç seviyesinden endüstriyel uygulamalara kadar her seviyede projeyi yapma imkanı sunuyor.
